# Fritzing sketch esp32cantransceiver (saved by Fritzing 1.0.6)
breadboards: 1

parts:
  M1 = SN65HVD230 CAN Bus transciever module [package=THT]
  S1 = Pushbutton [package="[THT]"]
  S2 = Pushbutton [package="[THT]"]
  S3 = Pushbutton [package="[THT]"]
  S4 = Pushbutton [package="[THT]"]
  U1 = POT [knob_status=50% power=0.5W package=pot_alpha_rv16af-20]
  U2 = POT [knob_status=50% power=0.5W package=pot_alpha_rv16af-20]
  CPU1 = NodeMCU WROOM ESP 32
  U3 = POT [knob_status=50% power=0.5W package=pot_alpha_rv16af-20]

nets:
  N1: M1.pin_1, U1.A, U2.A, CPU1.pin_17, U3.A
  N2: M1.pin_2, S1.Pin_3, S1.Pin_4, S2.Pin_3, S2.Pin_4, S3.Pin_3, S3.Pin_4, S4.Pin_3, S4.Pin_4, U1.E, U2.E, CPU1.pin_9, CPU1.pin_18, CPU1.pin_25, CPU1.pin_26, CPU1.pin_27, CPU1.pin_30, U3.E
  N3: M1.pin_3, CPU1.pin_8, CPU1.pin_24, CPU1.pin_28
  N4: M1.pin_4, CPU1.pin_21
  N5: M1.pin_5, M1.pin_6
  N6: S1.Pin_1, S1.Pin_2
  N7: S2.Pin_1, S2.Pin_2
  N8: S3.Pin_1, S3.Pin_2
  N9: S4.Pin_1, S4.Pin_2
  N10: U1.S, CPU1.pin_5
  N11: U2.S, CPU1.pin_6
  N12: CPU1.pin_7, U3.S

custom parts:
  SN65HVD230 CAN Bus transciever module: Bus Transceiver SN65HVD230 CAN Communication Module, for Arduino.
  NodeMCU WROOM ESP 32: 30 pol Development Kit
